// Logisim project CodCalculadoraTeclas.circ as structural Verilog: 1 circuit, main circuit main
module main (
  input  T0,
  input  T1,
  input  T2,
  input  T3,
  input  T4,
  input  T5,
  input  T6,
  input  T7,
  input  T8,
  input  T9
);

  wire [3:0] D_out;

  nand A (D_out[3], T8, T9);
  nand B (D_out[2], T4, T5, T6, T7);
  nand C (D_out[1], T2, T3, T6, T7);
  nand D (D_out[0], T1, T3, T5, T7, T9);
  // Probe on D_out
  // also tied to GND on the sheet: T0
endmodule
